# Fritzing sketch Wiring (saved by Fritzing 1.0.1rc)

parts:
  Raspberry_Pi_2 = Raspberry Pi 3 [part_number="ReRAM RPi"]
  Raspberry_Pi_1 = Raspberry Pi 3 [part_number="Supervisor RPi"]
  J3 = double row male pin header, 32 pins [form="♂ (male)"]  # not connected
  ReRAM_PCB = double row male pin header, 32 pins [form="♂ (male)"]  # not connected
  J2 = double row male pin header, 32 pins [form="♂ (male)"]
  J1 = double row male pin header, 32 pins [form="♂ (male)"]
  J5 = female pin header, 2 pins [form="♀ (female)"]  # not connected
  J6 = female pin header, 2 pins [form="♀ (female)"]  # not connected
  J7 = female pin header, 2 pins [form="♀ (female)"]  # not connected
  J8 = female pin header, 2 pins [form="♀ (female)"]  # not connected

nets:
  3V3: Raspberry_Pi_2.3v3, Raspberry_Pi_2.3V3, J2.pin4, J1.pin1
  GND: Raspberry_Pi_2.GND, Raspberry_Pi_1.GND, J2.pin6
  N1: Raspberry_Pi_2.GPIO10, J1.pin4
  N2: Raspberry_Pi_2.GPIO9, J2.pin3
  N3: Raspberry_Pi_2.GPIO11, J1.pin3
  N4: Raspberry_Pi_2.GPIO8, J2.pin2
  N5: Raspberry_Pi_2.GPIO25, J2.pin5
  N6: Raspberry_Pi_2.GPIO15, Raspberry_Pi_1.GPIO14
  N7: Raspberry_Pi_2.GPIO14, Raspberry_Pi_1.GPIO15

notes:
  3V
  GND
  PF6/CS!
